// Logisim project feataku.circ as structural Verilog: 2 circuits, main circuit main
module main (
  input  in_1,
  input  in_2,
  input  in_3,
  input  X,
  input  Y,
  input  CIn,
  output [3:0] out_7,
  output out_8,
  output S,
  output COut
);

  wire and_1_out, and_2_out, semisumador_1_s, xor_1_out;

  SemiSumador semisumador_1 (.X(in_1), .Y(in_2), .CIn(in_3), .S(semisumador_1_s), .COut(out_8));
  xor xor_1 (xor_1_out, X, Y);
  and and_1 (and_1_out, X, Y);
  xor xor_2 (S, xor_1_out, CIn);
  and and_2 (and_2_out, xor_1_out, CIn);
  xor xor_3 (COut, and_2_out, and_1_out);
endmodule

module SemiSumador (
  input  X,
  input  Y,
  input  CIn,
  output S,
  output COut
);

  wire and_1_out, and_2_out, xor_1_out;

  xor xor_1 (xor_1_out, X, Y);
  and and_1 (and_1_out, X, Y);
  xor xor_2 (S, xor_1_out, CIn);
  and and_2 (and_2_out, xor_1_out, CIn);
  xor xor_3 (COut, and_2_out, and_1_out);
endmodule
